// Logisim project adder.circ as structural Verilog: 2 circuits, main circuit main
module main (
  input  A,
  input  B,
  input  Cin,
  output S,
  output Cout
);

  wire C1, half_1_s, half_2_c;

  half half_1 (.A(A), .B(B), .S(half_1_s), .C(C1));
  // Probe on half_1_s
  half half_2 (.A(half_1_s), .B(Cin), .S(S), .C(half_2_c));
  or or_1 (Cout, C1, half_2_c);

  // Notes on the sheet:
  //   full adder
endmodule

module half (
  input  A,
  input  B,
  output S,
  output C
);

  xor xor_1 (S, A, B);
  and and_1 (C, B, A);
endmodule
