// Logisim project adder4-instances-grouped.circ as structural Verilog: 2 circuits, main circuit Adder4
module FullAdder (
  input  A,
  input  B,
  input  Cin,
  output S,
  output Cout
);

  wire and_1_out, and_2_out, xor_1_out;

  and and_1 (and_1_out, A, B);
  xor xor_1 (xor_1_out, A, B);
  xor xor_2 (S, xor_1_out, Cin);
  and and_2 (and_2_out, xor_1_out, Cin);
  or or_1 (Cout, and_1_out, and_2_out);
endmodule

module Adder4 (
  input  [3:0] A,
  input  [3:0] B,
  input  Cin,
  output [3:0] S,
  output Cout
);

  wire bit_0_cout, bit_1_cout, bit_2_cout;

  FullAdder bit_0 (.A(A[0]), .B(B[0]), .Cin(Cin), .S(S[0]), .Cout(bit_0_cout));
  FullAdder bit_1 (.A(A[1]), .B(B[1]), .Cin(bit_0_cout), .S(S[1]), .Cout(bit_1_cout));
  FullAdder bit_2 (.A(A[2]), .B(B[2]), .Cin(bit_1_cout), .S(S[2]), .Cout(bit_2_cout));
  FullAdder bit_3 (.A(A[3]), .B(B[3]), .Cin(bit_2_cout), .S(S[3]), .Cout(Cout));

  // Other names for the same wires on the sheet: bit_0_A = A[0]; bit_1_A = A[1]; bit_2_A = A[2]; bit_3_A = A[3];
  //   bit_0_B = B[0]; bit_1_B = B[1]; bit_2_B = B[2]; bit_3_B = B[3]; bit_0_S = S[0]; bit_1_S = S[1]; bit_2_S = S[2];
  //   bit_3_S = S[3]

  // Notes on the sheet:
  //   01  输入与拆分
  //   02  bit 0
  //   06  输出汇总
  //   03  bit 1
  //   04  bit 2
  //   05  bit 3
endmodule
