// Logisim project counter.circ as structural Verilog: 1 circuit, main circuit main
module main (
  input  EN,
  output Q0,
  output Q1,
  output Q2
);

  wire and_1_out, and_2_out, clock_1_out, xor_1_out, xor_2_out, xor_3_out;

  Clock #(.highDuration(1), .lowDuration(1)) clock_1 (.out(clock_1_out));
  xor xor_1 (xor_1_out, EN, Q0);
  and and_1 (and_1_out, EN, Q0);
  xor xor_2 (xor_2_out, and_1_out, Q1);
  and and_2 (and_2_out, and_1_out, Q1);
  xor xor_3 (xor_3_out, and_2_out, Q2);
  D_Flip_Flop #(.NegatePresetClear("false"), .NewFFLayout("true"), .Pre_Clr_Positions("ABOVE_BELOW"), .trigger("rising")) d_ff_1 (
    .clk(clock_1_out), .D(xor_1_out), .Q(Q0));  // open: Qn, preset, en, reset
  D_Flip_Flop #(.NegatePresetClear("false"), .NewFFLayout("true"), .Pre_Clr_Positions("ABOVE_BELOW"), .trigger("rising")) d_ff_2 (
    .clk(clock_1_out), .D(xor_2_out), .Q(Q1));  // open: Qn, preset, en, reset
  D_Flip_Flop #(.NegatePresetClear("false"), .NewFFLayout("true"), .Pre_Clr_Positions("ABOVE_BELOW"), .trigger("rising")) d_ff_3 (
    .clk(clock_1_out), .D(xor_3_out), .Q(Q2));  // open: Qn, preset, en, reset
endmodule
