// Logisim project decoder.circ as structural Verilog: 1 circuit, main circuit main
module main (
  input  EN,
  input  A1,
  input  A0,
  output Y0,
  output Y1,
  output Y2,
  output Y3
);

  wire not_1_out, not_2_out;

  not not_1 (not_1_out, A1);
  not not_2 (not_2_out, A0);
  and and_1 (Y0, EN, not_1_out, not_2_out);
  and and_2 (Y1, EN, not_1_out, A0);
  and and_3 (Y2, EN, A1, not_2_out);
  and and_4 (Y3, EN, A1, A0);
endmodule
