// Logisim project labels-on-wires.circ as structural Verilog: 2 circuits, main circuit before
module \before  (
  input  B,
  input  A,
  output T,
  output S
);

  not not_1 (T, B);
  not not_2 (S, A);
endmodule

module after (
  input  B,
  input  A,
  output T,
  output S
);

  not not_1 (T, B);
  not not_2 (S, A);
endmodule
