// Logisim project pins-off-side.circ as structural Verilog: 2 circuits, main circuit before
module \before  (
  input  A,
  output S
);

  not not_1 (S, A);
endmodule

module after (
  input  A,
  output S
);

  not not_1 (S, A);
endmodule
