// Logisim project ripple-fa.circ as structural Verilog: 2 circuits, main circuit main
module FullAdder (
  input  A,
  input  B,
  input  Cin,
  output S,
  output Cout
);

  wire and_1_out, and_2_out, xor_1_out;

  xor xor_1 (xor_1_out, A, B);
  xor xor_2 (S, xor_1_out, Cin);
  and and_1 (and_1_out, xor_1_out, Cin);
  and and_2 (and_2_out, A, B);
  or or_1 (Cout, and_1_out, and_2_out);
endmodule

module main (
  input  A0,
  input  B0,
  input  Cin,
  input  A1,
  input  B1,
  input  A2,
  input  B2,
  input  A3,
  input  B3,
  output S0,
  output S1,
  output S2,
  output S3,
  output Cout
);

  wire fulladder_1_cout, fulladder_2_cout, fulladder_3_cout;

  FullAdder fulladder_1 (.A(A0), .B(B0), .Cin(Cin), .S(S0), .Cout(fulladder_1_cout));
  FullAdder fulladder_2 (.A(A1), .B(B1), .Cin(fulladder_1_cout), .S(S1), .Cout(fulladder_2_cout));
  FullAdder fulladder_3 (.A(A2), .B(B2), .Cin(fulladder_2_cout), .S(S2), .Cout(fulladder_3_cout));
  FullAdder fulladder_4 (.A(A3), .B(B3), .Cin(fulladder_3_cout), .S(S3), .Cout(Cout));
endmodule
