// Logisim project bends.circ as structural Verilog: 2 circuits, main circuit before
module \before  (
  input  A
);

  // NOT_Gate not_1 has open pins: in=A, out=open
endmodule

module after (
  input  A
);

  // NOT_Gate not_1 has open pins: in=A, out=open
endmodule
