// Logisim project close-parallels.circ as structural Verilog: 2 circuits, main circuit before
module \before  (
  input  A,
  input  B
);

  // NOT_Gate not_1 has open pins: in=A, out=open
  // NOT_Gate not_2 has open pins: in=B, out=open
endmodule

module after (
  input  A,
  input  B
);

  // NOT_Gate not_1 has open pins: in=A, out=open
  // NOT_Gate not_2 has open pins: in=B, out=open
endmodule
