// Logisim project label-overlaps.circ as structural Verilog: 2 circuits, main circuit before
module \before  (
  input  A
);

  // NOT_Gate not_1 is placed but not wired
endmodule

module after (
  input  A
);

  // NOT_Gate not_1 is placed but not wired
endmodule
