// Logisim project overlaps.circ as structural Verilog: 2 circuits, main circuit before
module \before  (
);

  // AND_Gate and_1 is placed but not wired
  // OR_Gate or_1 is placed but not wired
endmodule

module after (
);

  // AND_Gate and_1 is placed but not wired
  // OR_Gate or_1 is placed but not wired
endmodule
