// Logisim project port-grazes.circ as structural Verilog: 2 circuits, main circuit before
module \before  (
  input  B,
  input  A,
  output S
);

  not not_1 (S, A);
  // NOT_Gate not_2 has open pins: in=B, out=open
endmodule

module after (
  input  B,
  input  A,
  output S
);

  not not_1 (S, A);
  // NOT_Gate not_2 has open pins: in=B, out=open
endmodule
