// Logisim project full-adder-wrong.circ as structural Verilog: 1 circuit, main circuit main
module main (
  input  A,
  input  B,
  input  Cin,
  output S,
  output Cout
);

  wire and_1_out, and_2_out;

  xor xor_1 (S, A, B);
  // XOR_Gate xor_2 has open pins: in0=S, in1=Cin, out=open
  and and_1 (and_1_out, S, Cin);
  and and_2 (and_2_out, A, B);
  or or_1 (Cout, and_1_out, and_2_out);
endmodule
